# Fritzing sketch rpi_arduino_servo (saved by Fritzing 0.8.7b)
breadboards: 1

parts:
  元件1 = Arduino Nano (Rev3.0)
  Raspberry_Pi_B_rev1 = Raspberry Pi B rev2
  Y_axis = Basic Servo
  X_axis = Basic Servo

nets:
  N1: 元件1.D0/RX, Raspberry_Pi_B_rev1.GPIO_14
  N2: 元件1.D9, X_axis.pulse
  N3: 元件1.D10, Y_axis.pulse
  5V: 元件1.5V, Y_axis.vcc, X_axis.vcc
  GND: Raspberry_Pi_B_rev1.GND, Y_axis.gnd, X_axis.gnd
